// Digital circuit register.dig as structural Verilog
module register (
  input  [7:0] s1,
  input  s1en,
  input  [7:0] s2,
  input  s2en,
  input  [7:0] s3,
  input  s3en,
  input  nC,
  input  Ld,
  input  en,
  output [7:0] Q
);

  wire and_1_out, and_2_out, and_3_out, not_1_out, not_2_out;
  wire [1:0] or_2_out;
  wire [7:0] multiplexer_1_out;

  Multiplexer #(.Selector_Bits(2), .Bits(8)) multiplexer_1 (
    .sel(or_2_out), .in_0(Q), .in_1(s1), .in_2(s2), .in_3(s3), .out(multiplexer_1_out));
  and and_1 (and_1_out, s1en, not_1_out);
  not not_1 (not_1_out, s2en);
  Register #(.Bits(8)) register_1 (.D(multiplexer_1_out), .C(nC), .en(and_2_out), .Q(Q));
  or or_1 (or_2_out[1], s2en, s3en);
  and and_2 (and_2_out, en, Ld);
  or or_2 (or_2_out[0], and_1_out, and_3_out);
  and and_3 (and_3_out, not_2_out, s3en);
  not not_2 (not_2_out, s2en);
endmodule
