// Digital circuit cpu.dig as structural Verilog
module cpu (
  input  clk,
  output [7:0] IR,
  output [7:0] Temp,
  output [7:0] PC,
  output [7:0] RA,
  output [7:0] RB
);

  wire CU_aluen, CU_aluop, CU_ir, CU_ld, CU_mem, CU_mv, CU_pc, CU_ra, CU_rb, CU_str, not_1_out;
  wire [7:0] eepromdualport_1_d, multiplexer_1_out, multiplexer_2_out;

  not not_1 (not_1_out, clk);
  cu_1 CU (
    .IRin(IR), .C(clk), .Str(CU_str), .Ld(CU_ld), .Mem(CU_mem), .Mv(CU_mv), .RA(CU_ra), .RB(CU_rb),
    .PC(CU_pc), .IR(CU_ir), .ALUen(CU_aluen), .ALUop(CU_aluop));
  LED Store (.in(CU_str));
  LED Load (.in(CU_ld));
  LED u_RA (.in(CU_ra));
  LED u_RB (.in(CU_rb));
  LED u_PC (.in(CU_pc));
  LED u_IR (.in(CU_ir));
  LED ALU (.in(CU_aluen));
  LED Sub (.in(CU_aluop));
  LED Memory (.in(CU_mv));
  Multiplexer #(.Bits(8)) multiplexer_1 (.sel(CU_pc), .in_0(Temp), .in_1(PC), .out(multiplexer_1_out));
  Counter #(.Bits(8)) counter_1 (.en(CU_pc), .C(not_1_out), .clr(1'b0), .out(PC));  // open: ovf
  Multiplexer #(.Bits(8)) multiplexer_2 (.sel(CU_rb), .in_0(RA), .in_1(RB), .out(multiplexer_2_out));
  register u_Temp (
    .nC(not_1_out), .en(CU_mv), .s1(RA), .s1en(CU_ra), .s2(RB), .s2en(CU_rb), .s3({3'b000, IR[4:0]}),
    .s3en(CU_ir), .Ld(CU_mv), .Q(Temp));
  register RA_2 (
    .nC(not_1_out), .en(CU_ra), .s1(Temp), .s1en(CU_ld), .s2(eepromdualport_1_d), .s2en(CU_mem),
    .s3({8{1'b0}}), .s3en(1'b0), .Ld(CU_ld), .Q(RA));
  register RB_2 (
    .nC(not_1_out), .en(CU_rb), .s1(Temp), .s1en(CU_ld), .s2(eepromdualport_1_d), .s2en(CU_mem),
    .s3({8{1'b0}}), .s3en(1'b0), .Ld(CU_ld), .Q(RB));
  register IR_2 (
    .nC(not_1_out), .en(CU_ir), .s1(eepromdualport_1_d), .s1en(CU_pc), .s2({8{1'b0}}), .s2en(1'b0),
    .s3({8{1'b0}}), .s3en(1'b0), .Ld(CU_ld), .Q(IR));
  EEPROMDualPort #(.AddrBits(8), .Bits(8)) eepromdualport_1 (
    .A(multiplexer_1_out), .Din(multiplexer_2_out), .str(CU_str), .C(clk), .ld(CU_ld), .D(eepromdualport_1_d));

  // Notes on the sheet:
  //   contents of eepromdualport_1 (hex, n*v repeats v):
  //   28,a2,29,0,0,2,0,0,3,8
endmodule
