// Digital circuit cu_1.dig as structural Verilog
module cu_1 (
  input  [7:0] IRin,
  input  C,
  output Str,
  output Ld,
  output Mem,
  output Mv,
  output RA,
  output RB,
  output PC,
  output IR,
  output ALUen,
  output ALUop
);

  wire ALUen1, ALUen2, ALUen_2_q, ALUen_3_q, ALUen_q, ALUop1, ALUop2, ALUop_2_q, ALUop_3_q, ALUop_q,
       and_1_out, and_2_out, and_3_out, and_4_out, C0_q, C1_q, C2_q, C3_q, C4_q, decoder_1_out_0,
       decoder_1_out_1, decoder_1_out_2, decoder_1_out_3, decoder_1_out_4, decoder_1_out_5, decoder_1_out_6,
       decoder_1_out_7, delay_1_out, delay_2_out, delay_3_out, delay_4_out, Ex1, Ex2, Ex_2_q, Ex_3_q, Ex_q,
       IR1, IR2, IR_2_q, IR_3_q, IR_q, Ld1, Ld2, Ld_2_q, Ld_3_q, Ld_q, Mem1, Mem2, Mem_2_q, Mem_3_q, Mem_q,
       multiplexer_1_out, multiplexer_2_out, multiplexer_3_out, multiplexer_4_out, multiplexer_5_out,
       multiplexer_6_out, multiplexer_7_out, multiplexer_8_out, multiplexer_9_out, multiplexer_10_out,
       multiplexer_11_out, multiplexer_12_out, multiplexer_13_out, multiplexer_14_out, multiplexer_15_out,
       multiplexer_16_out, multiplexer_17_out, multiplexer_18_out, multiplexer_19_out, multiplexer_20_out,
       multiplexer_21_out, multiplexer_22_out, multiplexer_23_out, multiplexer_24_out, multiplexer_25_out,
       multiplexer_26_out, multiplexer_27_out, multiplexer_28_out, multiplexer_29_out, multiplexer_30_out,
       multiplexer_31_out, multiplexer_32_out, multiplexer_33_out, multiplexer_34_out, multiplexer_35_out,
       multiplexer_36_out, multiplexer_37_out, Mv1, Mv2, Mv_2_q, Mv_3_q, Mv_q, not_1_out, not_2_out,
       or_9_out, or_11_out, or_15_out, or_16_out, or_27_out, or_28_out, PC1, PC2, PC_2_q, PC_3_q, PC_q, RA1,
       RA2, RA_2_q, RA_3_q, RA_q, RB1, RB2, RB_2_q, RB_3_q, RB_q, Str1, Str2, Str_2_q, Str_3_q, Str_q;

  Decoder #(.Selector_Bits(3)) decoder_1 (
    .sel(IRin[7:5]), .out_0(decoder_1_out_0), .out_1(decoder_1_out_1), .out_2(decoder_1_out_2),
    .out_3(decoder_1_out_3), .out_4(decoder_1_out_4), .out_5(decoder_1_out_5), .out_6(decoder_1_out_6),
    .out_7(decoder_1_out_7));
  or or_1 (PC1, 1'b0, 1'b0, 1'b0, 1'b0, 1'b0, 1'b0, 1'b0, 1'b0);
  or or_2 (PC2, 1'b0, 1'b0, 1'b0, 1'b0, 1'b0, 1'b0, 1'b0, 1'b0);
  or or_3 (Str1, 1'b0, 1'b0, 1'b0, 1'b0, 1'b0, 1'b0, 1'b0, 1'b0);
  or or_4 (Str2, 1'b0, 1'b0, 1'b0, decoder_1_out_4, decoder_1_out_3, 1'b0, 1'b0, 1'b0);
  or or_5 (Ld1, 1'b0, 1'b0, 1'b0, 1'b0, 1'b0, 1'b0, 1'b0, 1'b0);
  or or_6 (Ld2, 1'b0, 1'b0, decoder_1_out_5, 1'b0, 1'b0, decoder_1_out_2, decoder_1_out_1, 1'b0);
  or or_7 (Mem1, 1'b0, 1'b0, 1'b0, 1'b0, 1'b0, 1'b0, 1'b0, 1'b0);
  or or_8 (Mem2, 1'b0, 1'b0, 1'b0, decoder_1_out_4, decoder_1_out_3, decoder_1_out_2, decoder_1_out_1, 1'b0);
  or or_9 (or_9_out, decoder_1_out_2, decoder_1_out_5, decoder_1_out_4);
  or or_10 (Mv1, 1'b0, 1'b0, decoder_1_out_5, decoder_1_out_4, decoder_1_out_3, decoder_1_out_2, decoder_1_out_1, 1'b0);
  or or_11 (or_11_out, decoder_1_out_2, decoder_1_out_5, decoder_1_out_4);
  or or_12 (Mv2, 1'b0, 1'b0, 1'b0, 1'b0, 1'b0, 1'b0, 1'b0, 1'b0);
  not not_1 (not_1_out, IRin[0]);
  and and_1 (and_1_out, not_1_out, or_9_out);
  not not_2 (not_2_out, IRin[1]);
  and and_2 (and_2_out, not_2_out, or_11_out);
  or or_13 (RA1, 1'b0, 1'b0, 1'b0, 1'b0, 1'b0, and_1_out, 1'b0, 1'b0);
  or or_14 (RA2, 1'b0, 1'b0, 1'b0, 1'b0, decoder_1_out_3, and_2_out, decoder_1_out_1, 1'b0);
  or or_15 (or_15_out, decoder_1_out_2, decoder_1_out_5, decoder_1_out_4);
  and and_3 (and_3_out, IRin[0], or_15_out);
  or or_16 (or_16_out, decoder_1_out_2, decoder_1_out_5, decoder_1_out_4);
  and and_4 (and_4_out, IRin[1], or_16_out);
  or or_17 (RB1, 1'b0, 1'b0, 1'b0, 1'b0, 1'b0, and_3_out, 1'b0, 1'b0);
  or or_18 (RB2, 1'b0, 1'b0, 1'b0, 1'b0, 1'b0, and_4_out, 1'b0, 1'b0);
  or or_19 (IR1, 1'b0, 1'b0, 1'b0, 1'b0, decoder_1_out_3, 1'b0, decoder_1_out_1, 1'b0);
  or or_20 (IR2, 1'b0, 1'b0, 1'b0, 1'b0, 1'b0, 1'b0, 1'b0, 1'b0);
  or or_21 (Ex1, decoder_1_out_7, decoder_1_out_6, 1'b0, 1'b0, 1'b0, 1'b0, 1'b0, decoder_1_out_0);
  or or_22 (Ex2, 1'b0, 1'b0, decoder_1_out_5, decoder_1_out_4, decoder_1_out_3, decoder_1_out_2, decoder_1_out_1, 1'b0);
  or or_23 (ALUen1, decoder_1_out_7, decoder_1_out_6, 1'b0, 1'b0, 1'b0, 1'b0, 1'b0, 1'b0);
  or or_24 (ALUen2, 1'b0, 1'b0, 1'b0, 1'b0, 1'b0, 1'b0, 1'b0, 1'b0);
  or or_25 (ALUop1, decoder_1_out_7, 1'b0, 1'b0, 1'b0, 1'b0, 1'b0, 1'b0, 1'b0);
  or or_26 (ALUop2, 1'b0, 1'b0, 1'b0, 1'b0, 1'b0, 1'b0, 1'b0, 1'b0);
  Delay delay_1 (.in(C), .out(delay_1_out));
  Delay delay_2 (.in(C), .out(delay_2_out));
  Delay delay_3 (.in(C), .out(delay_3_out));
  Register C4 (.D(multiplexer_1_out), .C(delay_1_out), .en(delay_1_out), .Q(C4_q));
  Multiplexer multiplexer_1 (.sel(or_28_out), .in_0(C3_q), .in_1(1'b0), .out(multiplexer_1_out));
  Register C3 (.D(multiplexer_2_out), .C(delay_2_out), .en(delay_2_out), .Q(C3_q));
  Multiplexer multiplexer_2 (.sel(or_28_out), .in_0(C2_q), .in_1(1'b0), .out(multiplexer_2_out));
  Register C2 (.D(multiplexer_3_out), .C(delay_3_out), .en(delay_3_out), .Q(C2_q));
  Multiplexer multiplexer_3 (.sel(or_28_out), .in_0(C1_q), .in_1(1'b0), .out(multiplexer_3_out));
  Register C1 (.D(C0_q), .C(C), .en(C), .Q(C1_q));
  Register C0 (.D(multiplexer_4_out), .C(delay_4_out), .en(delay_4_out), .Q(C0_q));
  Multiplexer multiplexer_4 (.sel(or_27_out), .in_0(C), .in_1(1'b0), .out(multiplexer_4_out));
  Delay #(.delayTime(5)) delay_4 (.in(C), .out(delay_4_out));
  or or_27 (or_27_out, C4_q, C3_q, C2_q, C1_q, C0_q);
  or or_28 (or_28_out, multiplexer_37_out, multiplexer_26_out, multiplexer_15_out);
  Register u_PC (.D(PC1), .C(C1_q), .en(C1_q), .Q(PC_q));
  Register u_Str (.D(Str1), .C(C1_q), .en(C1_q), .Q(Str_q));
  Register u_Ld (.D(Ld1), .C(C1_q), .en(C1_q), .Q(Ld_q));
  Register u_Mem (.D(Mem1), .C(C1_q), .en(C1_q), .Q(Mem_q));
  Register u_Mv (.D(Mv1), .C(C1_q), .en(C1_q), .Q(Mv_q));
  Register u_RA (.D(RA1), .C(C1_q), .en(C1_q), .Q(RA_q));
  Register u_RB (.D(RB1), .C(C1_q), .en(C1_q), .Q(RB_q));
  Register u_IR (.D(IR1), .C(C1_q), .en(C1_q), .Q(IR_q));
  Register u_ALUen (.D(ALUen1), .C(C1_q), .en(C1_q), .Q(ALUen_q));
  Register u_ALUop (.D(ALUop1), .C(C1_q), .en(C1_q), .Q(ALUop_q));
  Register Ex (.D(Ex1), .C(C1_q), .en(C1_q), .Q(Ex_q));
  Multiplexer multiplexer_5 (.sel(C2_q), .in_0(1'b0), .in_1(PC_q), .out(multiplexer_5_out));
  Multiplexer multiplexer_6 (.sel(C2_q), .in_0(1'b0), .in_1(Str_q), .out(multiplexer_6_out));
  Multiplexer multiplexer_7 (.sel(C2_q), .in_0(1'b0), .in_1(Ld_q), .out(multiplexer_7_out));
  Multiplexer multiplexer_8 (.sel(C2_q), .in_0(1'b0), .in_1(Mem_q), .out(multiplexer_8_out));
  Multiplexer multiplexer_9 (.sel(C2_q), .in_0(1'b0), .in_1(Mv_q), .out(multiplexer_9_out));
  Multiplexer multiplexer_10 (.sel(C2_q), .in_0(1'b0), .in_1(RA_q), .out(multiplexer_10_out));
  Multiplexer multiplexer_11 (.sel(C2_q), .in_0(1'b0), .in_1(RB_q), .out(multiplexer_11_out));
  Multiplexer multiplexer_12 (.sel(C2_q), .in_0(1'b0), .in_1(IR_q), .out(multiplexer_12_out));
  Multiplexer multiplexer_13 (.sel(C2_q), .in_0(1'b0), .in_1(ALUen_q), .out(multiplexer_13_out));
  Multiplexer multiplexer_14 (.sel(C2_q), .in_0(1'b0), .in_1(ALUop_q), .out(multiplexer_14_out));
  Multiplexer multiplexer_15 (.sel(C2_q), .in_0(1'b0), .in_1(Ex_q), .out(multiplexer_15_out));
  or or_29 (PC, C0_q, multiplexer_5_out, multiplexer_16_out, multiplexer_27_out);
  Register PC_2 (.D(PC2), .C(C1_q), .en(C1_q), .Q(PC_2_q));
  Register Str_2 (.D(Str2), .C(C1_q), .en(C1_q), .Q(Str_2_q));
  Register Ld_2 (.D(Ld2), .C(C1_q), .en(C1_q), .Q(Ld_2_q));
  Register Mem_2 (.D(Mem2), .C(C1_q), .en(C1_q), .Q(Mem_2_q));
  Register Mv_2 (.D(Mv2), .C(C1_q), .en(C1_q), .Q(Mv_2_q));
  Register RA_2 (.D(RA2), .C(C1_q), .en(C1_q), .Q(RA_2_q));
  Register RB_2 (.D(RB2), .C(C1_q), .en(C1_q), .Q(RB_2_q));
  Register IR_2 (.D(IR2), .C(C1_q), .en(C1_q), .Q(IR_2_q));
  Register ALUen_2 (.D(ALUen2), .C(C1_q), .en(C1_q), .Q(ALUen_2_q));
  Register ALUop_2 (.D(ALUop2), .C(C1_q), .en(C1_q), .Q(ALUop_2_q));
  Register Ex_2 (.D(Ex2), .C(C1_q), .en(C1_q), .Q(Ex_2_q));
  or or_30 (Str, multiplexer_6_out, multiplexer_17_out, multiplexer_28_out);
  Multiplexer multiplexer_16 (.sel(C3_q), .in_0(1'b0), .in_1(PC_2_q), .out(multiplexer_16_out));
  Multiplexer multiplexer_17 (.sel(C3_q), .in_0(1'b0), .in_1(Str_2_q), .out(multiplexer_17_out));
  Multiplexer multiplexer_18 (.sel(C3_q), .in_0(1'b0), .in_1(Ld_2_q), .out(multiplexer_18_out));
  Multiplexer multiplexer_19 (.sel(C3_q), .in_0(1'b0), .in_1(Mem_2_q), .out(multiplexer_19_out));
  Multiplexer multiplexer_20 (.sel(C3_q), .in_0(1'b0), .in_1(Mv_2_q), .out(multiplexer_20_out));
  Multiplexer multiplexer_21 (.sel(C3_q), .in_0(1'b0), .in_1(RA_2_q), .out(multiplexer_21_out));
  Multiplexer multiplexer_22 (.sel(C3_q), .in_0(1'b0), .in_1(RB_2_q), .out(multiplexer_22_out));
  Multiplexer multiplexer_23 (.sel(C3_q), .in_0(1'b0), .in_1(IR_2_q), .out(multiplexer_23_out));
  Multiplexer multiplexer_24 (.sel(C3_q), .in_0(1'b0), .in_1(ALUen_2_q), .out(multiplexer_24_out));
  Multiplexer multiplexer_25 (.sel(C3_q), .in_0(1'b0), .in_1(ALUop_2_q), .out(multiplexer_25_out));
  Multiplexer multiplexer_26 (.sel(C3_q), .in_0(1'b0), .in_1(Ex_2_q), .out(multiplexer_26_out));
  or or_31 (Ld, C0_q, multiplexer_7_out, multiplexer_18_out, multiplexer_29_out);
  or or_32 (Mem, C0_q, multiplexer_8_out, multiplexer_19_out, multiplexer_30_out);
  or or_33 (Mv, C0_q, multiplexer_9_out, multiplexer_20_out, multiplexer_31_out);
  or or_34 (RA, multiplexer_10_out, multiplexer_21_out, multiplexer_32_out);
  Register PC_3 (.D(1'b0), .C(C1_q), .en(C1_q), .Q(PC_3_q));
  Register Str_3 (.D(1'b0), .C(C1_q), .en(C1_q), .Q(Str_3_q));
  Register Ld_3 (.D(1'b0), .C(C1_q), .en(C1_q), .Q(Ld_3_q));
  Register Mem_3 (.D(1'b0), .C(C1_q), .en(C1_q), .Q(Mem_3_q));
  Register Mv_3 (.D(1'b0), .C(C1_q), .en(C1_q), .Q(Mv_3_q));
  Register RA_3 (.D(1'b0), .C(C1_q), .en(C1_q), .Q(RA_3_q));
  Register RB_3 (.D(1'b0), .C(C1_q), .en(C1_q), .Q(RB_3_q));
  Register IR_3 (.D(1'b0), .C(C1_q), .en(C1_q), .Q(IR_3_q));
  Register ALUen_3 (.D(1'b0), .C(C1_q), .en(C1_q), .Q(ALUen_3_q));
  Register ALUop_3 (.D(1'b0), .C(C1_q), .en(C1_q), .Q(ALUop_3_q));
  Register Ex_3 (.D(1'b0), .C(C1_q), .en(C1_q), .Q(Ex_3_q));
  Multiplexer multiplexer_27 (.sel(C4_q), .in_0(PC_3_q), .in_1(1'b0), .out(multiplexer_27_out));
  Multiplexer multiplexer_28 (.sel(C4_q), .in_0(Str_3_q), .in_1(1'b0), .out(multiplexer_28_out));
  Multiplexer multiplexer_29 (.sel(C4_q), .in_0(Ld_3_q), .in_1(1'b0), .out(multiplexer_29_out));
  Multiplexer multiplexer_30 (.sel(C4_q), .in_0(Mem_3_q), .in_1(1'b0), .out(multiplexer_30_out));
  Multiplexer multiplexer_31 (.sel(C4_q), .in_0(Mv_3_q), .in_1(1'b0), .out(multiplexer_31_out));
  Multiplexer multiplexer_32 (.sel(C4_q), .in_0(RA_3_q), .in_1(1'b0), .out(multiplexer_32_out));
  Multiplexer multiplexer_33 (.sel(C4_q), .in_0(RB_3_q), .in_1(1'b0), .out(multiplexer_33_out));
  Multiplexer multiplexer_34 (.sel(C4_q), .in_0(IR_3_q), .in_1(1'b0), .out(multiplexer_34_out));
  Multiplexer multiplexer_35 (.sel(C4_q), .in_0(ALUen_3_q), .in_1(1'b0), .out(multiplexer_35_out));
  Multiplexer multiplexer_36 (.sel(C4_q), .in_0(ALUop_3_q), .in_1(1'b0), .out(multiplexer_36_out));
  Multiplexer multiplexer_37 (.sel(C4_q), .in_0(Ex_3_q), .in_1(1'b0), .out(multiplexer_37_out));
  or or_35 (RB, multiplexer_11_out, multiplexer_22_out, multiplexer_33_out);
  or or_36 (IR, C0_q, multiplexer_12_out, multiplexer_23_out, multiplexer_34_out);
  or or_37 (ALUen, multiplexer_35_out, multiplexer_24_out, multiplexer_13_out);
  or or_38 (ALUop, multiplexer_14_out, multiplexer_25_out, multiplexer_36_out);

  // Notes on the sheet:
  //   Decoder
  //   Control Logic
endmodule
